// Logisim project ALU32.circ as structural Verilog: 10 circuits, main circuit ALU32
module Add32 (
  input  [31:0] A,
  input  [31:0] B,
  input  Cin,
  output V,
  output [31:0] C
);

  wire adder16bits_1_cout, adder16bits_2_cout, adder16bits_2_overflow;

  Adder16bits adder16bits_1 (
    .B(B[15:0]), .A(A[15:0]), .Cin(Cin), .Cout(adder16bits_1_cout), .S(C[15:0]));  // open: overflow
  Adder16bits adder16bits_2 (
    .B(B[31:16]), .A(A[31:16]), .Cin(adder16bits_1_cout), .Cout(adder16bits_2_cout),
    .overflow(adder16bits_2_overflow), .S(C[31:16]));
  xor xor_1 (V, adder16bits_2_cout, adder16bits_2_overflow);
endmodule

module Adder1bit (
  input  A,
  input  B,
  input  Cin,
  output S,
  output Cout
);

  wire and_1_out, and_2_out, xor_1_out;

  xor xor_1 (xor_1_out, A, B);
  xor xor_2 (S, xor_1_out, Cin);
  and and_1 (and_1_out, xor_1_out, Cin);
  and and_2 (and_2_out, A, B);
  or or_1 (Cout, and_1_out, and_2_out);
endmodule

module Adder4bits (
  input  [3:0] A,
  input  [3:0] B,
  input  Cin,
  output Cout,
  output overflow,
  output [3:0] S
);

  wire adder1bit_1_cout, adder1bit_2_cout;

  Adder1bit adder1bit_1 (.Cout(adder1bit_1_cout), .Cin(Cin), .S(S[0]), .A(A[0]), .B(B[0]));
  Adder1bit adder1bit_2 (.Cout(adder1bit_2_cout), .Cin(adder1bit_1_cout), .S(S[1]), .A(A[1]), .B(B[1]));
  Adder1bit adder1bit_3 (.Cout(overflow), .Cin(adder1bit_2_cout), .S(S[2]), .A(A[2]), .B(B[2]));
  Adder1bit adder1bit_4 (.Cout(Cout), .Cin(overflow), .S(S[3]), .A(A[3]), .B(B[3]));
endmodule

module Adder16bits (
  input  [15:0] B,
  input  [15:0] A,
  input  Cin,
  output Cout,
  output overflow,
  output [15:0] S
);

  wire adder4bits_1_cout, adder4bits_2_cout, adder4bits_3_cout;

  Adder4bits adder4bits_1 (.Cout(adder4bits_1_cout), .Cin(Cin), .S(S[3:0]), .B(B[3:0]), .A(A[3:0]));  // open: overflow
  Adder4bits adder4bits_2 (
    .Cout(adder4bits_2_cout), .Cin(adder4bits_1_cout), .S(S[7:4]), .B(B[7:4]), .A(A[7:4]));  // open: overflow
  Adder4bits adder4bits_3 (
    .Cout(adder4bits_3_cout), .Cin(adder4bits_2_cout), .S(S[11:8]), .B(B[11:8]), .A(A[11:8]));  // open: overflow
  Adder4bits adder4bits_4 (
    .Cout(Cout), .Cin(adder4bits_3_cout), .S(S[15:12]), .B(B[15:12]), .A(A[15:12]), .overflow(overflow));
endmodule

module LeftShift32 (
  input  Cin,
  input  [31:0] B,
  input  [4:0] Sa,
  output [31:0] C
);

  wire [31:0] multiplexer_1_out, multiplexer_2_out, multiplexer_3_out, multiplexer_4_out;

  Multiplexer #(.width(32), .enable("false")) multiplexer_1 (
    .in0(B), .in1({B[30:0], Cin}), .out(multiplexer_1_out), .sel(Sa[0]));
  Multiplexer #(.width(32), .enable("false")) multiplexer_2 (
    .in0(multiplexer_1_out), .in1({multiplexer_1_out[29:0], {2{Cin}}}), .out(multiplexer_2_out), .sel(Sa[1]));
  Multiplexer #(.width(32), .enable("false")) multiplexer_3 (
    .in0(multiplexer_2_out), .in1({multiplexer_2_out[27:0], {4{Cin}}}), .out(multiplexer_3_out), .sel(Sa[2]));
  Multiplexer #(.width(32), .enable("false")) multiplexer_4 (
    .in0(multiplexer_3_out), .in1({multiplexer_3_out[23:0], {8{Cin}}}), .out(multiplexer_4_out), .sel(Sa[3]));
  Multiplexer #(.width(32), .enable("false")) multiplexer_5 (
    .in0(multiplexer_4_out), .in1({multiplexer_4_out[15:0], {16{Cin}}}), .out(C), .sel(Sa[4]));
endmodule

module ALU32 (
  input  [31:0] A,
  input  [31:0] B,
  input  [3:0] Op,
  input  [4:0] Sa,
  output [31:0] C,
  output V
);

  wire and_1_out, and_2_out;
  wire [31:0] add32_1_c, and_3_out, and_4_out, bit_extender_1_out, comparealu_1_c, gatealu_1_c,
       multiplexer_1_out, not_1_out, shift_1_c;

  Multiplexer #(.width(32), .enable("false")) multiplexer_1 (
    .in0(B), .in1(not_1_out), .out(multiplexer_1_out), .sel(Op[2]));
  assign not_1_out = ~B;  // NOT_Gate not_1, 32 bits wide
  and and_1 (and_1_out, ~Op[1], Op[3]);  // AND_Gate
  assign bit_extender_1_out = {{31{and_1_out}}, and_1_out};  // Bit_Extender bit_extender_1
  and and_2 (and_2_out, and_1_out, Op[2]);
  assign and_3_out = A & bit_extender_1_out;  // AND_Gate and_3, 32 bits wide
  assign and_4_out = bit_extender_1_out & multiplexer_1_out;  // AND_Gate and_4, 32 bits wide
  GateALU gatealu_1 (.A(A), .B(B), .Op(Op), .C(gatealu_1_c));
  CompareALU comparealu_1 (.B(B), .A(A), .Op(Op), .C(comparealu_1_c));
  Add32 add32_1 (.A(and_3_out), .B(and_4_out), .Cin(and_2_out), .V(V), .C(add32_1_c));
  Shift shift_1 (.B(B), .Op(Op), .Sa(Sa), .C(shift_1_c));
  assign C = gatealu_1_c | comparealu_1_c | add32_1_c | shift_1_c;  // OR_Gate or_1, 32 bits wide
  // AND_Gate and_5 is placed but not wired

  // Notes on the sheet:
  //   Op
  //   A
  //   B
  //   B
  //   B
  //   B
  //   A
  //   Op
  //   If not add or sub Op, input 0
  //   Choose B or ~B
  //   A
  //   Divide the function of ALU into four parts
  //   Asserted if Op is 110x
  //   All other unasserted parts will produce a 32 bit 0
  //   Use a 32 bits OR gate to produce the output
endmodule

module GateALU (
  input  [31:0] A,
  input  [31:0] B,
  input  [3:0] Op,
  output [31:0] C
);

  wire and_1_out;
  wire [31:0] and_2_out, nor_1_out, or_1_out, xor_1_out;

  and and_1 (and_1_out, Op[0], ~Op[3]);  // AND_Gate
  assign or_1_out = A | B;  // OR_Gate or_1, 32 bits wide
  assign and_2_out = A & B;  // AND_Gate and_2, 32 bits wide
  assign nor_1_out = ~(A | B);  // NOR_Gate nor_1, 32 bits wide
  assign xor_1_out = A ^ B;  // XOR_Gate xor_1, 32 bits wide
  Multiplexer #(.select(2), .width(32)) multiplexer_1 (
    .in0(or_1_out), .in1(and_2_out), .in2(nor_1_out), .in3(xor_1_out), .out(C), .sel(Op[2:1]), .en(and_1_out));

  // Notes on the sheet:
  //   If not gate Op, output 0 to C
endmodule

module CompareALU (
  input  [31:0] B,
  input  [31:0] A,
  input  [3:0] Op,
  output [31:0] C
);

  wire and_3_out, and_6_out, and_7_out, and_8_out, not_2_out, not_3_out;
  wire [1:0] and_1_out, and_2_out, and_2_out_2, and_2_out_3, and_2_out_4, and_5_out;
  wire [7:0] and_4_out;
  wire [31:0] bit_extender_1_out, bit_extender_2_out, bit_extender_3_out, bit_extender_4_out, not_1_out,
       xnor_1_out;

  assign not_1_out = ~A;  // NOT_Gate not_1, 32 bits wide
  assign xnor_1_out = ~(B ^ A);  // XNOR_Gate xnor_1, 32 bits wide
  assign and_1_out = and_2_out & and_2_out_2 & and_2_out_3 & and_2_out_4;  // AND_Gate and_1, 2 bits wide
  assign {and_2_out_4, and_2_out_3, and_2_out_2, and_2_out} = not_1_out[7:0] & not_1_out[15:8] & not_1_out[23:16] & not_1_out[31:24];  // AND_Gate and_2, 8 bits wide
  and and_3 (and_3_out, ~Op[0], ~Op[3]);  // AND_Gate
  assign and_4_out = xnor_1_out[7:0] & xnor_1_out[15:8] & xnor_1_out[23:16] & xnor_1_out[31:24];  // AND_Gate and_4, 8 bits wide
  assign and_5_out = and_4_out[1:0] & and_4_out[3:2] & and_4_out[5:4] & and_4_out[7:6];  // AND_Gate and_5, 2 bits wide
  and and_6 (and_6_out, and_1_out[0], and_1_out[1]);
  and and_7 (and_7_out, and_5_out[0], and_5_out[1]);
  and and_8 (and_8_out, ~A[31], ~and_6_out);  // AND_Gate
  not not_2 (not_2_out, and_7_out);
  not not_3 (not_3_out, and_8_out);
  assign bit_extender_1_out = {{31{1'b0}}, not_2_out};  // Bit_Extender bit_extender_1
  assign bit_extender_2_out = {{31{1'b0}}, and_7_out};  // Bit_Extender bit_extender_2
  assign bit_extender_3_out = {{31{1'b0}}, not_3_out};  // Bit_Extender bit_extender_3
  assign bit_extender_4_out = {{31{1'b0}}, and_8_out};  // Bit_Extender bit_extender_4
  Multiplexer #(.select(2), .width(32)) multiplexer_1 (
    .in0(bit_extender_1_out), .in1(bit_extender_2_out), .in2(bit_extender_3_out), .in3(bit_extender_4_out),
    .out(C), .sel(Op[2:1]), .en(and_3_out));

  // Notes on the sheet:
  //   If A==B, A XOR B =0
  //   If A>0, A 31th bit will be 0
  //   If A>0, at least 1 bit (0-30th) will be 1
  //   If not compare Op, output 0 to C
endmodule

module Shift (
  input  [31:0] B,
  input  [3:0] Op,
  input  [4:0] Sa,
  output [31:0] C
);

  wire and_1_out, and_2_out, and_3_out, mirror_1_signbit;
  wire [4:0] and_4_out, bit_extender_1_out;
  wire [31:0] leftshift32_1_c, mirror_1_b_mirror, mirror_2_b_mirror, multiplexer_1_out;

  Mirror mirror_1 (.B(B), .B_Mirror(mirror_1_b_mirror), .SignBit(mirror_1_signbit));
  and and_1 (and_1_out, Op[1], Op[3]);
  and and_2 (and_2_out, mirror_1_signbit, Op[0]);
  Multiplexer #(.width(32)) multiplexer_1 (
    .in0(B), .in1(mirror_1_b_mirror), .out(multiplexer_1_out), .sel(Op[2]), .en(and_1_out));
  and and_3 (and_3_out, and_2_out, Op[2]);
  assign bit_extender_1_out = {{4{and_1_out}}, and_1_out};  // Bit_Extender bit_extender_1
  assign and_4_out = bit_extender_1_out & Sa;  // AND_Gate and_4, 5 bits wide
  LeftShift32 leftshift32_1 (.Cin(and_3_out), .B(multiplexer_1_out), .Sa(and_4_out), .C(leftshift32_1_c));
  Multiplexer #(.width(32), .enable("false")) multiplexer_2 (
    .in0(leftshift32_1_c), .in1(mirror_2_b_mirror), .out(C), .sel(Op[2]));
  Mirror mirror_2 (.B(leftshift32_1_c), .B_Mirror(mirror_2_b_mirror));  // open: SignBit

  // Notes on the sheet:
  //   Choose mirror ot not
  //   Input the sign bit if Op is 1111
  //   If not shift Op, input 0 to Sa
  //   If not shift Op, output 0 to C
  //   Choose mirror ot not
endmodule

module Mirror (
  input  [31:0] B,
  output [31:0] B_Mirror,
  output SignBit
);


  assign B_Mirror = {B[0], B[1], B[2], B[3], B[4], B[5], B[6], B[7], B[8], B[9], B[10], B[11], B[12], B[13], B[14], B[15], B[16], B[17], B[18], B[19], B[20], B[21], B[22], B[23], B[24], B[25], B[26], B[27], B[28], B[29], B[30], B[31]};
  assign SignBit = B[31];

  // Notes on the sheet:
  //   To big so use a sub circuit.
endmodule
